# Fritzing sketch rpi-green-led (saved by Fritzing 0.9.3b)
breadboards: 1

parts:
  Raspberry_Pi_1 = Raspberry Pi 3 [part_number=RPI-3-V1.2]
  R1 = Resistor [tolerance=±5% resistance=220 package="2512 [SMD]"]
  LED1 = smd LED [color="Green (555nm)" package="1206 [SMD]"]

nets:
  N1: Raspberry_Pi_1.GIPO18, LED1.anode
  N2: Raspberry_Pi_1.GND, R1.Pin_1
  N3: R1.Pin_0, LED1.cathode
