# Fritzing sketch rpi-green-led-blue-button-red-button-blue-led (saved by Fritzing 0.9.3b)
breadboards: 1

parts:
  Raspberry_Pi_1 = Raspberry Pi 3 [part_number=RPI-3-V1.2]
  R1 = Resistor [tolerance=±5% resistance=220 package="2512 [SMD]"]
  LED1 = smd LED [color="Green (555nm)" package="1206 [SMD]"]
  R2 = Resistor [tolerance=±5% resistance=10k package="2512 [SMD]"]
  S1 = Pushbutton [package="[SMD]"]
  R3 = Resistor [tolerance=±5% resistance=10k package="2512 [SMD]"]
  S2 = Pushbutton [package="[SMD]"]
  R4 = Resistor [tolerance=±5% resistance=220 package="2512 [SMD]"]
  LED2 = smd LED [color="Blue (430nm)" package="1206 [SMD]"]

nets:
  N1: Raspberry_Pi_1.3v3, R2.Pin_1, R3.Pin_1
  N2: Raspberry_Pi_1.GIPO16, LED2.anode
  N3: Raspberry_Pi_1.GIPO12, R3.Pin_0, S2.Pin_3, S2.Pin_4
  N4: Raspberry_Pi_1.GIPO25, R2.Pin_0, S1.Pin_3, S1.Pin_4
  N5: Raspberry_Pi_1.GIPO18, LED1.anode
  N6: Raspberry_Pi_1.GND, R1.Pin_1, S1.Pin_1, S1.Pin_2, S2.Pin_1, S2.Pin_2, R4.Pin_1
  N7: R1.Pin_0, LED1.cathode
  N8: R4.Pin_0, LED2.cathode

notes:
  Blue Button
  Red Button
